# Fritzing sketch cooker (saved by Fritzing 0.8.5b)
breadboards: 1

parts:
  LCD1 = LCD screen
  Part1 = Arduino Uno (Rev3)
  R1 = Rotary Potentiometer (Small) [maximum_resistance=100kΩ package=THT]

nets:
  VSS: LCD1.VSS, Part1.GND, R1.leg2
  VDD: LCD1.VDD, LCD1.LED+, LCD1.LED-, Part1.5V, R1.leg1
  N1: LCD1.V0, R1.wiper
  N2: LCD1.RS, Part1.D12/MISO
  N3: LCD1.R/W, Part1.D11_PWM/MOSI
  N4: LCD1.E, Part1.D10_PWM/SS
  N5: LCD1.DB4, Part1.D5_PWM
  N6: LCD1.DB5, Part1.D4
  N7: LCD1.DB6, Part1.D3_PWM
  N8: LCD1.DB7, Part1.D2
